// Logisim project hw4.circ as structural Verilog: 5 circuits, main circuit main
module main (
  input  X,
  output out_2
);

  wire clock_out, reset_out, S0_prime_out_5, S0_q, S1_prime_out_5, S1_q, S2_prime_y, S2_q;

  Clock clock (.out(clock_out));
  Button reset (.out(reset_out));
  D_Flip_Flop S2 (.clk(clock_out), .D(S2_prime_y), .Q(S2_q), .reset(reset_out));  // open: Qn, preset, en
  D_Flip_Flop S1 (.clk(clock_out), .D(S1_prime_out_5), .Q(S1_q), .reset(reset_out));  // open: Qn, preset, en
  S2 S2_prime (.s2(S2_q), .s1(S1_q), .s0(S0_q), .x(X), .y(S2_prime_y));
  S1 S1_prime (.s2(S2_q), .s1(S1_q), .s0(S0_q), .x(X), .out_5(S1_prime_out_5));
  S0 S0_prime (.s2(S2_q), .s1(S1_q), .s0(S0_q), .x(X), .out_5(S0_prime_out_5));
  z Z (.s2(S2_q), .s1(S1_q), .s0(S0_q), .x(X), .out_5(out_2));
  D_Flip_Flop S0 (.clk(clock_out), .D(S0_prime_out_5), .Q(S0_q), .reset(reset_out));  // open: Qn, preset, en
endmodule

module S2 (
  input  s2,
  input  s1,
  input  s0,
  input  x,
  output y
);

  wire and_1_out, and_2_out;

  and and_1 (and_1_out, ~s2, s1, ~x);  // AND_Gate
  and and_2 (and_2_out, s2, ~s0, x);  // AND_Gate
  or or_1 (y, and_1_out, and_2_out);
endmodule

module S1 (
  input  s2,
  input  s1,
  input  s0,
  input  x,
  output out_5
);

  wire or_1_out, or_2_out;

  or or_1 (or_1_out, s1, ~x);  // OR_Gate
  or or_2 (or_2_out, ~s2, ~s0, ~x);  // OR_Gate
  and and_1 (out_5, or_1_out, or_2_out);
endmodule

module S0 (
  input  s2,
  input  s1,
  input  s0,
  input  x,
  output out_5
);

  wire or_1_out, or_2_out;

  or or_1 (or_1_out, s2, ~s1);  // OR_Gate
  or or_2 (or_2_out, s0, x);
  and and_1 (out_5, or_1_out, or_2_out);
endmodule

module z (
  input  s2,
  input  s1,
  input  s0,
  input  x,
  output out_5
);

  wire and_1_out, and_2_out;

  and and_1 (and_1_out, ~s2, s1, ~s0, ~x);  // AND_Gate
  and and_2 (and_2_out, s1, s0, x);
  or or_1 (out_5, and_1_out, and_2_out);
endmodule
